// Logisim project branch-comp.circ as structural Verilog: 1 circuit, main circuit branch_comp
module branch_comp (
  input  [31:0] BrData1,
  input  [31:0] BrData2,
  input  BrUn,
  output BrEq,
  output BrLt
);

  wire BrEq_signed, BrEq_unsigned, BrLt_signed, BrLt_unsigned;

  Comparator #(.mode("unsigned"), .width(32)) comparator_1 (
    .a(BrData1), .b(BrData2), .eq(BrEq_unsigned), .lt(BrLt_unsigned));  // open: gt
  Comparator #(.width(32)) comparator_2 (.a(BrData1), .b(BrData2), .eq(BrEq_signed), .lt(BrLt_signed));  // open: gt
  Multiplexer multiplexer_1 (.in0(BrEq_signed), .in1(BrEq_unsigned), .out(BrEq), .sel(BrUn));
  Multiplexer multiplexer_2 (.in0(BrLt_signed), .in1(BrLt_unsigned), .out(BrLt), .sel(BrUn));

  // Notes on the sheet:
  //   INPUTS to your circuit
  //   DON'T CHANGE THE LOCATIONS OF THE INPUTS AND OUTPUTS!
  //   OUTPUT from your circuit
endmodule
