// Logisim project control-logic.circ as structural Verilog: 3 circuits, main circuit control_logic
module control_logic (
  input  [31:0] Instruction,
  input  BrEq,
  input  BrLt,
  output PCSel,
  output RegWEn,
  output [2:0] ImmSel,
  output BrUn,
  output ASel,
  output BSel,
  output [3:0] ALUSel,
  output MemWEn,
  output [1:0] WBSel
);

  wire and_1_out, and_2_out, and_3_out, and_4_out, and_5_out, and_6_out, B, BrUn0, BrUn1, comparator_10_eq,
       comparator_11_eq, comparator_12_eq, comparator_13_eq, comparator_16_eq, comparator_17_eq,
       comparator_18_eq, comparator_19_eq, comparator_20_eq, comparator_21_eq, comparator_22_eq, I, I_0, I_1,
       J, not_1_out, not_2_out, not_3_out, PCSelOn_B, PCSelOn_I, priority_encoder_1_gs, R, S, U_0, U_1;
  wire [2:0] priority_encoder_1_out, priority_encoder_2_out, priority_encoder_3_out;
  wire [5:0] i1_control_logic_1_out_3, multiplexer_1_out, multiplexer_2_out, multiplexer_3_out,
       r_control_logic_1_out_3, ROM_input, undriven, undriven_2, undriven_3, undriven_4;
  wire [15:4] rom_1_data;

  Comparator #(.width(7)) comparator_1 (.a(7'b0110011), .b(Instruction[6:0]), .eq(R));  // open: gt, lt
  Comparator #(.width(7)) comparator_2 (.a(7'b0000011), .b(Instruction[6:0]), .eq(I_0));  // open: gt, lt
  Comparator #(.width(7)) comparator_3 (.a(7'b0010011), .b(Instruction[6:0]), .eq(I_1));  // open: gt, lt
  Comparator #(.width(7)) comparator_4 (.a(7'b0100011), .b(Instruction[6:0]), .eq(S));  // open: gt, lt
  Comparator #(.width(7)) comparator_5 (.a(7'b1100011), .b(Instruction[6:0]), .eq(B));  // open: gt, lt
  Comparator #(.width(7)) comparator_6 (.a(7'b0010111), .b(Instruction[6:0]), .eq(U_0));  // open: gt, lt
  Comparator #(.width(7)) comparator_7 (.a(7'b0110111), .b(Instruction[6:0]), .eq(U_1));  // open: gt, lt
  Comparator #(.width(7)) comparator_8 (.a(7'b1101111), .b(Instruction[6:0]), .eq(J));  // open: gt, lt
  Comparator #(.width(7)) comparator_9 (.a(7'b1100111), .b(Instruction[6:0]), .eq(I));  // open: gt, lt
  ROM #(.addrWidth(6), .dataWidth(16)) rom_1 (
    .addr(ROM_input),
    .data({rom_1_data[15:14], WBSel, MemWEn, ALUSel, BSel, ASel, rom_1_data[4], ImmSel, RegWEn}));
  Comparator #(.width(3)) comparator_10 (.a(3'b000), .b(Instruction[14:12]), .eq(comparator_10_eq));  // open: gt, lt
  Comparator #(.width(3)) comparator_11 (.a(3'b001), .b(Instruction[14:12]), .eq(comparator_11_eq));  // open: gt, lt
  not not_1 (not_1_out, BrEq);
  Comparator #(.width(3)) comparator_12 (.a(3'b100), .b(Instruction[14:12]), .eq(comparator_12_eq));  // open: gt, lt
  Comparator #(.width(3)) comparator_13 (.a(3'b101), .b(Instruction[14:12]), .eq(comparator_13_eq));  // open: gt, lt
  not not_2 (not_2_out, BrLt);
  Comparator #(.width(3)) comparator_14 (.a(3'b110), .b(Instruction[14:12]), .eq(BrUn0));  // open: gt, lt
  Comparator #(.width(3)) comparator_15 (.a(3'b111), .b(Instruction[14:12]), .eq(BrUn1));  // open: gt, lt
  not not_3 (not_3_out, BrLt);
  and and_1 (and_1_out, comparator_10_eq, BrEq);
  and and_2 (and_2_out, comparator_11_eq, not_1_out);
  and and_3 (and_3_out, comparator_12_eq, BrLt);
  and and_4 (and_4_out, comparator_13_eq, not_2_out);
  and and_5 (and_5_out, BrUn0, BrLt);
  and and_6 (and_6_out, BrUn1, not_3_out);
  Priority_Encoder priority_encoder_1 (
    .in1(and_1_out), .in2(and_2_out), .in3(and_3_out), .in4(and_4_out), .in5(and_5_out), .in6(and_6_out),
    .out(priority_encoder_1_out), .gs(priority_encoder_1_gs));  // open: in0, in7, en_in, en_out
  R_control_logic r_control_logic_1 (
    .in_1(Instruction[14:12]), .in_2(Instruction[31:25]), .out_3(r_control_logic_1_out_3));
  I1_control_logic i1_control_logic_1 (
    .in_1(Instruction[14:12]), .in_2(Instruction[31:25]), .out_3(i1_control_logic_1_out_3));
  assign ROM_input = R ? r_control_logic_1_out_3 : 6'bz;  // Controlled_Buffer controlled_buffer_1
  assign ROM_input = I_1 ? i1_control_logic_1_out_3 : 6'bz;  // Controlled_Buffer controlled_buffer_2
  Multiplexer #(.select(3), .width(6)) multiplexer_1 (
    .in1(6'b011010), .in2(6'b011011), .in3(6'b011100), .in4(6'b011101), .in5(6'b011110), .in6(6'b011111),
    .out(multiplexer_1_out), .sel(priority_encoder_1_out));  // open: in0, in7
  Comparator #(.width(3)) comparator_16 (.a(3'b000), .b(Instruction[14:12]), .eq(comparator_16_eq));  // open: gt, lt
  Comparator #(.width(3)) comparator_17 (.a(3'b001), .b(Instruction[14:12]), .eq(comparator_17_eq));  // open: gt, lt
  Comparator #(.width(3)) comparator_18 (.a(3'b010), .b(Instruction[14:12]), .eq(comparator_18_eq));  // open: gt, lt
  Comparator #(.width(3)) comparator_19 (.a(3'b000), .b(Instruction[14:12]), .eq(comparator_19_eq));  // open: gt, lt
  Comparator #(.width(3)) comparator_20 (.a(3'b001), .b(Instruction[14:12]), .eq(comparator_20_eq));  // open: gt, lt
  Comparator #(.width(3)) comparator_21 (.a(3'b010), .b(Instruction[14:12]), .eq(comparator_21_eq));  // open: gt, lt
  Comparator #(.width(3)) comparator_22 (.a(3'b000), .b(Instruction[14:12]), .eq(comparator_22_eq));  // open: gt, lt
  Priority_Encoder priority_encoder_2 (
    .in0(comparator_16_eq), .in1(comparator_17_eq), .in2(comparator_18_eq), .out(priority_encoder_2_out));  // open: in3, in4, in5, in6, in7, en_in, gs, en_out
  Priority_Encoder priority_encoder_3 (
    .in0(comparator_19_eq), .in1(comparator_20_eq), .in2(comparator_21_eq), .out(priority_encoder_3_out));  // open: in3, in4, in5, in6, in7, en_in, gs, en_out
  assign ROM_input = U_0 ? 6'b100000 : 6'bz;  // Controlled_Buffer controlled_buffer_3
  assign ROM_input = U_1 ? 6'b100001 : 6'bz;  // Controlled_Buffer controlled_buffer_4
  assign ROM_input = J ? 6'b100010 : 6'bz;  // Controlled_Buffer controlled_buffer_5
  assign ROM_input = PCSelOn_I ? 6'b100011 : 6'bz;  // Controlled_Buffer controlled_buffer_6
  and and_7 (PCSelOn_I, comparator_22_eq, I);
  assign ROM_input = PCSelOn_B ? multiplexer_1_out : 6'bz;  // Controlled_Buffer controlled_buffer_7
  and and_8 (PCSelOn_B, B, priority_encoder_1_gs);
  or or_1 (BrUn, BrUn0, BrUn1);
  assign ROM_input = I_0 ? multiplexer_2_out : 6'bz;  // Controlled_Buffer controlled_buffer_8
  Multiplexer #(.select(3), .width(6)) multiplexer_2 (
    .in0(6'b001100), .in1(6'b001101), .in2(6'b001110), .in4(undriven), .in6(undriven_2),
    .out(multiplexer_2_out), .sel(priority_encoder_2_out));  // open: in3, in5, in7
  Multiplexer #(.select(3), .width(6)) multiplexer_3 (
    .in0(6'b010111), .in1(6'b011000), .in2(6'b011001), .in4(undriven_3), .in6(undriven_4),
    .out(multiplexer_3_out), .sel(priority_encoder_3_out));  // open: in3, in5, in7
  or or_2 (PCSel, PCSelOn_B, J, PCSelOn_I);
  assign ROM_input = S ? multiplexer_3_out : 6'bz;  // Controlled_Buffer controlled_buffer_9

  // Other names for the same wires on the sheet: opcode[6:0] = Instruction[6:0]; funct3[2:0] = Instruction[14:12];
  //   funct7[6:0] = Instruction[31:25]; PCSelOn_J = J

  // Notes on the sheet:
  //   INPUTS to your circuit
  //   Connect ROM Input here ->
  //   rd
  //   rs1
  //   rs2
  //   imm
  //   contents of rom_1 (hex, n*v repeats v):
  //   1001 1401 1601 1081 1481 1581 1101 1201 1281 1681 1301 1381 41 41 41 1041 10c1 1141 1241 12c1 16c1
  //   1341 13c1 842 842 842 4*64 74 74 1067 17c7 3069 3041
  //   beq
  //   bne
  //   blt
  //   bge
  //   bltu
  //   bgeu
  //   ROM FOR CONTROL LOGIC
  //   BrUn seems like complication
  //   DON'T CHANGE THE LOCATIONS OF THE INPUTS AND OUTPUTS!
  //   This is only if you choose to do the ROM option
  //   OUTPUT from your circuit
  //   https://docs.google.com/spreadsheets/d/19MkohNO2yCCk6rRMd5Y-KDsqoHkXe3wCx7QYsCBHFKQ/view#gid=0
  //   https://docs.google.com/spreadsheets/d/1vts9_fcR0R5lcWhoOKzbi-m19LdhPlSol3BM-b1i-8Q/edit#gid=1550641118
  //   Reminder: If using ROM, use combinational logic for PCSel
  //   most likely unnecessary
endmodule

module R_control_logic (
  input  [2:0] in_1,
  input  [6:0] in_2,
  output [5:0] out_3
);

  wire and_1_out, and_2_out, and_3_out, and_4_out, and_5_out, and_6_out, and_7_out, and_8_out, and_9_out,
       and_10_out, and_11_out, and_12_out, comparator_1_eq, comparator_2_eq, comparator_3_eq,
       comparator_4_eq, comparator_5_eq, comparator_6_eq, comparator_7_eq, comparator_8_eq, comparator_9_eq,
       comparator_10_eq, comparator_11_eq, comparator_12_eq, comparator_13_eq, comparator_14_eq,
       comparator_15_eq, comparator_16_eq, comparator_17_eq, comparator_18_eq, comparator_19_eq,
       comparator_20_eq, comparator_21_eq, comparator_22_eq, comparator_23_eq, comparator_24_eq;

  Comparator #(.width(3)) comparator_1 (.a(3'b000), .b(in_1), .eq(comparator_1_eq));  // open: gt, lt
  Comparator #(.width(3)) comparator_2 (.a(3'b000), .b(in_1), .eq(comparator_2_eq));  // open: gt, lt
  Comparator #(.width(3)) comparator_3 (.a(3'b000), .b(in_1), .eq(comparator_3_eq));  // open: gt, lt
  Comparator #(.width(3)) comparator_4 (.a(3'b001), .b(in_1), .eq(comparator_4_eq));  // open: gt, lt
  Comparator #(.width(3)) comparator_5 (.a(3'b001), .b(in_1), .eq(comparator_5_eq));  // open: gt, lt
  Comparator #(.width(3)) comparator_6 (.a(3'b011), .b(in_1), .eq(comparator_6_eq));  // open: gt, lt
  Comparator #(.width(3)) comparator_7 (.a(3'b010), .b(in_1), .eq(comparator_7_eq));  // open: gt, lt
  Comparator #(.width(3)) comparator_8 (.a(3'b100), .b(in_1), .eq(comparator_8_eq));  // open: gt, lt
  Comparator #(.width(3)) comparator_9 (.a(3'b101), .b(in_1), .eq(comparator_9_eq));  // open: gt, lt
  Comparator #(.width(3)) comparator_10 (.a(3'b101), .b(in_1), .eq(comparator_10_eq));  // open: gt, lt
  Comparator #(.width(3)) comparator_11 (.a(3'b110), .b(in_1), .eq(comparator_11_eq));  // open: gt, lt
  Comparator #(.width(3)) comparator_12 (.a(3'b111), .b(in_1), .eq(comparator_12_eq));  // open: gt, lt
  Comparator #(.width(7)) comparator_13 (.a({7{1'b0}}), .b(in_2), .eq(comparator_13_eq));  // open: gt, lt
  Comparator #(.width(7)) comparator_14 (.a(7'b0000001), .b(in_2), .eq(comparator_14_eq));  // open: gt, lt
  Comparator #(.width(7)) comparator_15 (.a(7'b0100000), .b(in_2), .eq(comparator_15_eq));  // open: gt, lt
  Comparator #(.width(7)) comparator_16 (.a({7{1'b0}}), .b(in_2), .eq(comparator_16_eq));  // open: gt, lt
  Comparator #(.width(7)) comparator_17 (.a(7'b0000001), .b(in_2), .eq(comparator_17_eq));  // open: gt, lt
  Comparator #(.width(7)) comparator_18 (.a(7'b0000001), .b(in_2), .eq(comparator_18_eq));  // open: gt, lt
  Comparator #(.width(7)) comparator_19 (.a({7{1'b0}}), .b(in_2), .eq(comparator_19_eq));  // open: gt, lt
  Comparator #(.width(7)) comparator_20 (.a({7{1'b0}}), .b(in_2), .eq(comparator_20_eq));  // open: gt, lt
  Comparator #(.width(7)) comparator_21 (.a({7{1'b0}}), .b(in_2), .eq(comparator_21_eq));  // open: gt, lt
  Comparator #(.width(7)) comparator_22 (.a(7'b0100000), .b(in_2), .eq(comparator_22_eq));  // open: gt, lt
  Comparator #(.width(7)) comparator_23 (.a({7{1'b0}}), .b(in_2), .eq(comparator_23_eq));  // open: gt, lt
  Comparator #(.width(7)) comparator_24 (.a({7{1'b0}}), .b(in_2), .eq(comparator_24_eq));  // open: gt, lt
  and and_1 (and_1_out, comparator_1_eq, comparator_13_eq);
  and and_2 (and_2_out, comparator_2_eq, comparator_14_eq);
  and and_3 (and_3_out, comparator_3_eq, comparator_15_eq);
  and and_4 (and_4_out, comparator_4_eq, comparator_16_eq);
  and and_5 (and_5_out, comparator_5_eq, comparator_17_eq);
  and and_6 (and_6_out, comparator_6_eq, comparator_18_eq);
  and and_7 (and_7_out, comparator_7_eq, comparator_19_eq);
  and and_8 (and_8_out, comparator_8_eq, comparator_20_eq);
  and and_9 (and_9_out, comparator_9_eq, comparator_21_eq);
  and and_10 (and_10_out, comparator_10_eq, comparator_22_eq);
  and and_11 (and_11_out, comparator_11_eq, comparator_23_eq);
  and and_12 (and_12_out, comparator_12_eq, comparator_24_eq);
  Priority_Encoder #(.select_enc(4)) priority_encoder_1 (
    .in0(and_1_out), .in1(and_2_out), .in2(and_3_out), .in3(and_4_out), .in4(and_5_out), .in5(and_6_out),
    .in6(and_7_out), .in7(and_8_out), .in8(and_9_out), .in9(and_10_out), .in10(and_11_out),
    .in11(and_12_out), .out(out_3[3:0]));  // open: in12, in13, in14, in15, gs, en_out, en_in

  assign out_3[5:4] = 2'b00;

  // Other names for the same wires on the sheet: funct3[2:0] = in_1; funct7[6:0] = in_2
endmodule

module I1_control_logic (
  input  [2:0] in_1,
  input  [6:0] in_2,
  output [5:0] out_3
);

  wire and_1_out, and_2_out, and_3_out, comparator_1_eq, comparator_2_eq, comparator_3_eq, comparator_4_eq,
       comparator_5_eq, comparator_6_eq, comparator_7_eq, comparator_8_eq, comparator_9_eq, comparator_10_eq,
       comparator_11_eq;
  wire [3:0] priority_encoder_1_out;

  Comparator #(.width(3)) comparator_1 (.a(3'b000), .b(in_1), .eq(comparator_1_eq));  // open: gt, lt
  Comparator #(.width(3)) comparator_2 (.a(3'b001), .b(in_1), .eq(comparator_2_eq));  // open: gt, lt
  Comparator #(.width(3)) comparator_3 (.a(3'b010), .b(in_1), .eq(comparator_3_eq));  // open: gt, lt
  Comparator #(.width(3)) comparator_4 (.a(3'b100), .b(in_1), .eq(comparator_4_eq));  // open: gt, lt
  Comparator #(.width(3)) comparator_5 (.a(3'b101), .b(in_1), .eq(comparator_5_eq));  // open: gt, lt
  Comparator #(.width(3)) comparator_6 (.a(3'b101), .b(in_1), .eq(comparator_6_eq));  // open: gt, lt
  Comparator #(.width(3)) comparator_7 (.a(3'b110), .b(in_1), .eq(comparator_7_eq));  // open: gt, lt
  Comparator #(.width(3)) comparator_8 (.a(3'b111), .b(in_1), .eq(comparator_8_eq));  // open: gt, lt
  Comparator #(.width(7)) comparator_9 (.a({7{1'b0}}), .b(in_2), .eq(comparator_9_eq));  // open: gt, lt
  Comparator #(.width(7)) comparator_10 (.a({7{1'b0}}), .b(in_2), .eq(comparator_10_eq));  // open: gt, lt
  Comparator #(.width(7)) comparator_11 (.a(7'b0100000), .b(in_2), .eq(comparator_11_eq));  // open: gt, lt
  and and_1 (and_1_out, comparator_2_eq, comparator_9_eq);
  and and_2 (and_2_out, comparator_5_eq, comparator_10_eq);
  and and_3 (and_3_out, comparator_6_eq, comparator_11_eq);
  Priority_Encoder #(.select_enc(4)) priority_encoder_1 (
    .in0(comparator_1_eq), .in1(and_1_out), .in2(comparator_3_eq), .in3(comparator_4_eq), .in4(and_2_out),
    .in5(and_3_out), .in6(comparator_7_eq), .in7(comparator_8_eq), .out(priority_encoder_1_out));  // open: in8, in9, in10, in11, in12, in13, in14, in15, gs, en_out, en_in
  Adder #(.width(6)) adder_1 (.a({2'b00, priority_encoder_1_out}), .b(6'b001111), .out(out_3));  // open: cin, cout

  // Other names for the same wires on the sheet: funct3[2:0] = in_1; funct7[6:0] = in_2
endmodule
