// Logisim project cpu.circ as structural Verilog: 1 circuit, main circuit cpu
module cpu (
  input  clk,
  input  [31:0] Instruction,
  input  [31:0] MemReadData,
  output [31:0] MemAddress,
  output [31:0] ProgramCounter,
  output [31:0] ra,
  output [31:0] sp,
  output [31:0] t0,
  output [31:0] t1,
  output [31:0] t2,
  output [31:0] s0,
  output [31:0] s1,
  output [31:0] a0,
  output [3:0] MemWriteMask,
  output [31:0] MemWriteData
);

  wire ASel, BrEq, BrLt, BrUn, BSel, MemWen, PCSel, PCSel_IMEM, RegWEn, undriven;
  wire [1:0] WBSel;
  wire [2:0] ImmSel;
  wire [3:0] AluSel;
  wire [31:0] adder_2_out, ALU_result_IMEM, Imm, Instruction_t, MemData, multiplexer_1_out,
       multiplexer_2_out, multiplexer_3_out, multiplexer_4_out, PC_plus4, PC_plus4_IMEM, ProgramCounter_t,
       ReadData1, ReadData2, WBData;

  Register #(.width(32)) ALU_IMEM (.D(MemAddress), .clk(clk), .Q(ALU_result_IMEM));  // open: en, clr
  Register #(.width(1)) u_PCSel_IMEM (.D(PCSel), .clk(clk), .Q(PCSel_IMEM));  // open: en, clr
  Adder #(.width(32)) adder_1 (.a(ProgramCounter), .b(32'h4), .out(PC_plus4_IMEM));  // open: cin, cout
  Register #(.width(32)) PC (.D(multiplexer_1_out), .clk(clk), .Q(ProgramCounter));  // open: en, clr
  Multiplexer #(.width(32)) multiplexer_1 (.in0(PC_plus4_IMEM), .in1(MemAddress), .out(multiplexer_1_out), .sel(PCSel));
  Register #(.width(32)) Other_PC (.D(ProgramCounter), .clk(clk), .Q(ProgramCounter_t));  // open: en, clr
  Register #(.width(32)) Other_Instruction (
    .D(multiplexer_2_out), .clk(clk), .Q(Instruction_t), .clr(undriven));  // open: en
  Multiplexer #(.width(32)) multiplexer_2 (.in0(Instruction), .in1({32{1'b0}}), .out(multiplexer_2_out), .sel(PCSel));
  control_logic control_logic_1 (
    .Instruction(Instruction_t), .BrEq(BrEq), .BrLt(BrLt), .PCSel(PCSel), .RegWEn(RegWEn), .ImmSel(ImmSel),
    .BrUn(BrUn), .ASel(ASel), .BSel(BSel), .ALUSel(AluSel), .MemWEn(MemWen), .WBSel(WBSel));
  imm_gen imm_gen_1 (.Instruction(Instruction_t), .ImmSel(ImmSel), .Immediate(Imm));
  regfile regfile_1 (
    .ReadIndex1(Instruction_t[19:15]), .ReadIndex2(Instruction_t[24:20]), .WriteIndex(Instruction_t[11:7]),
    .WriteData(WBData), .RegWEn(RegWEn), .clk(clk), .ra(ra), .sp(sp), .t0(t0), .t1(t1), .t2(t2), .s0(s0),
    .s1(s1), .a0(a0), .ReadData1(ReadData1), .ReadData2(ReadData2));
  branch_comp branch_comp_1 (.BrData1(ReadData1), .BrData2(ReadData2), .BrUn(BrUn), .BrEq(BrEq), .BrLt(BrLt));
  Multiplexer #(.width(32)) multiplexer_3 (
    .in0(ReadData1), .in1(ProgramCounter_t), .out(multiplexer_3_out), .sel(ASel));
  Multiplexer #(.width(32)) multiplexer_4 (.in0(ReadData2), .in1(Imm), .out(multiplexer_4_out), .sel(BSel));
  alu alu_1 (.A(multiplexer_3_out), .B(multiplexer_4_out), .ALUSel(AluSel), .ALUResult(MemAddress));
  partial_store partial_store_1 (
    .Instruction(Instruction_t), .MemAddress(MemAddress), .DataFromReg(ReadData2), .MemWEn(MemWen),
    .MemWriteMask(MemWriteMask), .DataToMem(MemWriteData));
  partial_load partial_load_1 (
    .Instruction(Instruction_t), .MemAddress(MemAddress), .DataFromMem(MemReadData), .DataToReg(MemData));
  Adder #(.width(32)) adder_2 (.a(ProgramCounter_t), .b(32'h4), .out(adder_2_out));  // open: cin, cout
  Multiplexer #(.select(2), .width(32)) multiplexer_5 (
    .in0(MemData), .in1(MemAddress), .in2(ProgramCounter_t), .in3(PC_plus4), .out(WBData), .sel(WBSel));
  Multiplexer #(.width(32)) multiplexer_6 (.in0(adder_2_out), .in1(MemAddress), .out(PC_plus4), .sel(PCSel));

  // Other names for the same wires on the sheet: ALU_result[31:0] = MemAddress; Imem_Instruction[31:0] = Instruction;
  //   rd[4:0] = Instruction_t[11:7]; rs1[4:0] = Instruction_t[19:15]; rs2[4:0] = Instruction_t[24:20];
  //   PC_IMEM[31:0] = ProgramCounter

  // Notes on the sheet:
  //   Branch hazard!
  //   Alu_res (n-1) -> ALU_IMEM, instruction other - 0
  //   To IMEM
  //   IMEM Stage
  //   IMEM (do **NOT** move this)
  //   opcode
  //   funct3
  //   funct7
  //   From IMEM
  //   Could I run without
  //   Cashes
  //   Memory stores/loads
  //   Inputs/Outputs for testing. Do **NOT** move these.
  //   Parallel stuff with vectors like in GPUs
  //   It is OK to move the PC, RegFile, ALU, MEM, Branch Comp, Imm Gen, Partial Load, Partial Store and Control Logic to wherever is most convenient for you when constructing your CPU, and to delete this text
  //   Pipelining, speed of cycles, delays
  //   To DMEM
  //   DMEM (do **NOT** move this)
  //   From DMEM
  //   is this pc sel needed here?
endmodule
