// Logisim project imm-gen.circ as structural Verilog: 1 circuit, main circuit imm_gen
module imm_gen (
  input  [31:0] Instruction,
  input  [2:0] ImmSel,
  output [31:0] Immediate
);

  wire B, I, J, S, U;
  wire [11:0] multiplexer_5_out;
  wire [19:0] multiplexer_3_out, multiplexer_4_out;
  wire [20:0] multiplexer_1_out, multiplexer_2_out;

  Comparator #(.width(3)) comparator_1 (.a(ImmSel), .b(3'b000), .eq(I));  // open: gt, lt
  Comparator #(.width(3)) comparator_2 (.a(ImmSel), .b(3'b001), .eq(S));  // open: gt, lt
  Comparator #(.width(3)) comparator_3 (.a(ImmSel), .b(3'b010), .eq(B));  // open: gt, lt
  Comparator #(.width(3)) comparator_4 (.a(ImmSel), .b(3'b011), .eq(U));  // open: gt, lt
  Comparator #(.width(3)) comparator_5 (.a(ImmSel), .b(3'b100), .eq(J));  // open: gt, lt
  Multiplexer #(.width(21)) multiplexer_1 (
    .in0({21{1'b0}}), .in1({21{1'b1}}), .out(multiplexer_1_out), .sel(Instruction[31]));
  Multiplexer #(.width(21)) multiplexer_2 (
    .in0({21{1'b0}}), .in1({21{1'b1}}), .out(multiplexer_2_out), .sel(Instruction[31]));
  Multiplexer #(.width(20)) multiplexer_3 (
    .in0({20{1'b0}}), .in1({20{1'b1}}), .out(multiplexer_3_out), .sel(Instruction[31]));
  Multiplexer #(.width(20)) multiplexer_4 (
    .in0({20{1'b0}}), .in1({20{1'b1}}), .out(multiplexer_4_out), .sel(Instruction[31]));
  Multiplexer #(.width(12)) multiplexer_5 (
    .in0({12{1'b0}}), .in1({12{1'b1}}), .out(multiplexer_5_out), .sel(Instruction[31]));
  assign Immediate = I ? {multiplexer_1_out, Instruction[30:20]} : 32'bz;  // Controlled_Buffer controlled_buffer_1
  assign Immediate = S ? {multiplexer_2_out, Instruction[30:25], Instruction[11:7]} : 32'bz;  // Controlled_Buffer controlled_buffer_2
  assign Immediate = B ? {multiplexer_3_out, Instruction[7], Instruction[30:25], Instruction[11:8], 1'b0} : 32'bz;  // Controlled_Buffer controlled_buffer_3
  assign Immediate = U ? {Instruction[31:12], {12{1'b0}}} : 32'bz;  // Controlled_Buffer controlled_buffer_4
  assign Immediate = J ? {multiplexer_5_out, Instruction[19:12], Instruction[20], Instruction[30:21], 1'b0} : 32'bz;  // Controlled_Buffer controlled_buffer_5

  // Other names for the same wires on the sheet: negative = Instruction[31]; elvthB = Instruction[7];
  //   Jto[9:0] = Instruction[30:21]; elvthJ = Instruction[20]

  // Notes on the sheet:
  //   J
  //   INPUTS to your circuit
  //   I type
  //   S type
  //   B
  //   U
  //   11:7 rd
  //   11:7 rd
  //   14:12 funct3
  //   11:7 rd
  //   14:12 funct3
  //   19:15 rs1
  //   31:20 immidiate[11:0]
  //   19:15 rs1
  //   31:20 immidiate[11:0]
  //   14:12 funct3
  //   DON'T CHANGE THE LOCATIONS OF THE INPUTS AND OUTPUTS!
  //   OUTPUT from your circuit
endmodule
