// Logisim project partial-load.circ as structural Verilog: 1 circuit, main circuit partial_load
module partial_load (
  input  [31:0] Instruction,
  input  [31:0] MemAddress,
  input  [31:0] DataFromMem,
  output [31:0] DataToReg
);

  wire and_1_out, and_4_out, comparator_1_eq, comparator_2_eq, comparator_3_eq, first_byte, first_halfword,
       not_1_out;
  wire [1:0] priority_encoder_1_out;
  wire [31:0] DataByte, DataHalfword;

  Comparator #(.width(3)) comparator_1 (.a(3'b000), .b(Instruction[14:12]), .eq(comparator_1_eq));  // open: gt, lt
  Comparator #(.width(3)) comparator_2 (.a(3'b001), .b(Instruction[14:12]), .eq(comparator_2_eq));  // open: gt, lt
  Comparator #(.width(3)) comparator_3 (.a(3'b010), .b(Instruction[14:12]), .eq(comparator_3_eq));  // open: gt, lt
  Priority_Encoder #(.select_enc(2)) priority_encoder_1 (
    .in0(comparator_1_eq), .in1(comparator_2_eq), .in2(comparator_3_eq), .out(priority_encoder_1_out));  // open: in3, gs, en_out, en_in
  Multiplexer #(.select(2), .width(32)) multiplexer_1 (
    .in0(DataByte), .in1(DataHalfword), .in2(DataFromMem), .out(DataToReg), .sel(priority_encoder_1_out));  // open: in3
  Multiplexer #(.select(2), .width(8)) multiplexer_2 (
    .in0(DataFromMem[7:0]), .in1(DataFromMem[15:8]), .in2(DataFromMem[23:16]), .in3(DataFromMem[31:24]),
    .out(DataByte[7:0]), .sel(MemAddress[1:0]));
  Multiplexer #(.width(24)) multiplexer_3 (.in0({24{1'b0}}), .in1({24{1'b1}}), .out(DataByte[31:8]), .sel(and_4_out));
  Multiplexer #(.select(2), .width(16)) multiplexer_4 (
    .in0(DataFromMem[15:0]), .in1(DataFromMem[23:8]), .in2(DataFromMem[31:16]), .out(DataHalfword[15:0]),
    .sel(MemAddress[1:0]));  // open: in3
  Multiplexer #(.width(16)) multiplexer_5 (
    .in0({16{1'b0}}), .in1({16{1'b1}}), .out(DataHalfword[31:16]), .sel(and_1_out));
  not not_1 (not_1_out, MemAddress[0]);
  and and_1 (and_1_out, first_halfword, DataFromMem[31]);
  and and_2 (first_halfword, not_1_out, MemAddress[1]);
  and and_3 (first_byte, MemAddress[1], MemAddress[0]);
  and and_4 (and_4_out, first_byte, DataFromMem[31]);

  // Other names for the same wires on the sheet: negative = DataFromMem[31]; funct3[2:0] = Instruction[14:12];
  //   BottomBits[1:0] = MemAddress[1:0]

  // Notes on the sheet:
  //   INPUTS to your circuit
  //   DON'T CHANGE THE LOCATIONS OF THE INPUTS AND OUTPUTS!
  //   Bottom 2 bits?
  //   OUTPUT from your circuit
endmodule
