// Logisim project partial-store.circ as structural Verilog: 1 circuit, main circuit partial_store
module partial_store (
  input  [31:0] Instruction,
  input  [31:0] MemAddress,
  input  [31:0] DataFromReg,
  input  MemWEn,
  output [3:0] MemWriteMask,
  output [31:0] DataToMem
);

  wire comparator_1_eq, comparator_2_eq, comparator_3_eq, comparator_4_eq, comparator_5_eq, comparator_6_eq,
       not_1_out;
  wire [1:0] priority_encoder_1_out, priority_encoder_2_out;
  wire [3:0] MaskByte;
  wire [3:1] MaskHalfword;
  wire [31:0] DataByte, DataHalfword;

  Comparator #(.width(3)) comparator_1 (.a(3'b000), .b(Instruction[14:12]), .eq(comparator_1_eq));  // open: gt, lt
  Comparator #(.width(3)) comparator_2 (.a(3'b001), .b(Instruction[14:12]), .eq(comparator_2_eq));  // open: gt, lt
  Comparator #(.width(3)) comparator_3 (.a(3'b010), .b(Instruction[14:12]), .eq(comparator_3_eq));  // open: gt, lt
  Priority_Encoder #(.select_enc(2)) priority_encoder_1 (
    .in0(comparator_1_eq), .in1(comparator_2_eq), .in2(comparator_3_eq), .out(priority_encoder_1_out));  // open: in3, gs, en_out, en_in
  Demultiplexer #(.select(2), .width(8)) demultiplexer_1 (
    .out0(DataByte[7:0]), .out1(DataByte[15:8]), .out2(DataByte[23:16]), .out3(DataByte[31:24]),
    .in(DataFromReg[7:0]), .sel(MemAddress[1:0]));
  Demultiplexer #(.select(2), .width(16)) demultiplexer_2 (
    .out0(DataHalfword[15:0]), .out2(DataHalfword[31:16]), .in(DataFromReg[15:0]), .sel(MemAddress[1:0]));  // open: out1, out3
  Multiplexer #(.select(2), .width(32)) multiplexer_1 (
    .in0(DataByte), .in1(DataHalfword), .in2(DataFromReg), .out(DataToMem), .sel(priority_encoder_1_out));  // open: in3
  Decoder #(.select(2)) decoder_1 (
    .out0(MaskByte[0]), .out1(MaskByte[1]), .out2(MaskByte[2]), .out3(MaskByte[3]), .sel(MemAddress[1:0]));  // open: en
  Decoder #(.select(2)) decoder_2 (
    .out0(MaskHalfword[1]), .out2(MaskHalfword[3]), .sel(MemAddress[1:0]));  // open: out1, out3, en
  Comparator #(.width(3)) comparator_4 (.a(3'b000), .b(Instruction[14:12]), .eq(comparator_4_eq));  // open: gt, lt
  Comparator #(.width(3)) comparator_5 (.a(3'b001), .b(Instruction[14:12]), .eq(comparator_5_eq));  // open: gt, lt
  Comparator #(.width(3)) comparator_6 (.a(3'b010), .b(Instruction[14:12]), .eq(comparator_6_eq));  // open: gt, lt
  Priority_Encoder #(.select_enc(2)) priority_encoder_2 (
    .in0(comparator_4_eq), .in1(comparator_5_eq), .in2(comparator_6_eq), .in3(not_1_out),
    .out(priority_encoder_2_out));  // open: gs, en_out, en_in
  not not_1 (not_1_out, MemWEn);
  Multiplexer #(.select(2), .width(4)) multiplexer_2 (
    .in0(MaskByte), .in1({{2{MaskHalfword[3]}}, {2{MaskHalfword[1]}}}), .in2(4'b1111), .in3(4'b0000),
    .out(MemWriteMask), .sel(priority_encoder_2_out));

  // Other names for the same wires on the sheet: funct3[2:0] = Instruction[14:12];
  //   MaskHalfword (some bits) = {MaskHalfword[3], MaskHalfword[1]}; BottomBits[1:0] = MemAddress[1:0]

  // Notes on the sheet:
  //   INPUTS to your circuit
  //   Bottom 2 bits?
  //   DON'T CHANGE THE LOCATIONS OF THE INPUTS AND OUTPUTS!
  //   OUTPUT from your circuit
endmodule
