// Logisim project regfile.circ as structural Verilog: 1 circuit, main circuit regfile
module regfile (
  input  [4:0] ReadIndex1,
  input  [4:0] ReadIndex2,
  input  [4:0] WriteIndex,
  input  [31:0] WriteData,
  input  RegWEn,
  input  clk,
  output [31:0] ra,
  output [31:0] sp,
  output [31:0] t0,
  output [31:0] t1,
  output [31:0] t2,
  output [31:0] s0,
  output [31:0] s1,
  output [31:0] a0,
  output [31:0] ReadData1,
  output [31:0] ReadData2
);

  wire a0_on, ra_on, s0_on, s1_on, sp_on, t0_on, t1_on, t2_on, x0_on;

  Decoder #(.select(5)) decoder_1 (
    .out0(x0_on), .out1(ra_on), .out2(sp_on), .out5(t0_on), .out6(t1_on), .out7(t2_on), .out8(s0_on),
    .out9(s1_on), .out10(a0_on), .sel(WriteIndex), .en(RegWEn));  // open: out3, out4, out11, out12, out13, out14, out15, out16, out17, out18, out19, out20, out21, out22, out23, out24, out25, out26, out27, out28, out29, out30, out31
  Register #(.width(32)) register_1 (.D(WriteData), .en(ra_on), .clk(clk), .Q(ra));  // open: clr
  Register #(.width(32)) register_2 (.D(WriteData), .en(sp_on), .clk(clk), .Q(sp));  // open: clr
  Register #(.width(32)) register_3 (.D(WriteData), .en(t0_on), .clk(clk), .Q(t0));  // open: clr
  Register #(.width(32)) register_4 (.D(WriteData), .en(t1_on), .clk(clk), .Q(t1));  // open: clr
  Register #(.width(32)) register_5 (.D(WriteData), .en(t2_on), .clk(clk), .Q(t2));  // open: clr
  Register #(.width(32)) register_6 (.D(WriteData), .en(s0_on), .clk(clk), .Q(s0));  // open: clr
  Register #(.width(32)) register_7 (.D(WriteData), .en(s1_on), .clk(clk), .Q(s1));  // open: clr
  Register #(.width(32)) register_8 (.D(WriteData), .en(a0_on), .clk(clk), .Q(a0));  // open: clr
  Multiplexer #(.select(5), .width(32)) multiplexer_1 (
    .in0({32{1'b0}}), .in1(ra), .in2(sp), .in5(t0), .in6(t1), .in7(t2), .in8(s0), .in9(s1), .in10(a0),
    .out(ReadData1), .sel(ReadIndex1));  // open: in3, in4, in11, in12, in13, in14, in15, in16, in17, in18, in19, in20, in21, in22, in23, in24, in25, in26, in27, in28, in29, in30, in31
  Multiplexer #(.select(5), .width(32)) multiplexer_2 (
    .in0({32{1'b0}}), .in1(ra), .in2(sp), .in5(t0), .in6(t1), .in7(t2), .in8(s0), .in9(s1), .in10(a0),
    .out(ReadData2), .sel(ReadIndex2));  // open: in3, in4, in11, in12, in13, in14, in15, in16, in17, in18, in19, in20, in21, in22, in23, in24, in25, in26, in27, in28, in29, in30, in31

  // Other names for the same wires on the sheet: a0_x10[31:0] = a0; ra_x1[31:0] = ra; s0_x8[31:0] = s0;
  //   s1_x9[31:0] = s1; sp_x2[31:0] = sp; t0_x5[31:0] = t0; t1_x6[31:0] = t1; t2_x7[31:0] = t2
endmodule
